# Fritzing sketch light (saved by Fritzing 0.9.2b)
circuit board: 7cm x 4.3cm

parts:
  Adafruit_HUZZAH_ESP8266_Breakout1 = Adafruit HUZZAH ESP8266 Breakout [part_number=2471]
  U1 = Voltage Regulator - 3.3V [package="TO220 [THT]"]
  Q5 = npn-Powertransistor [package="TO220 [THT]"]
  LED1 = RGB LED (com. anode, rbg) [package="5 mm [THT]"]  # not connected
  R1 = Resistor [tolerance=±5% resistance=3.3 package=THT]
  R2 = Resistor [tolerance=±5% resistance=2.2 package=THT]
  R3 = Resistor [tolerance=±5% resistance=2.2 package=THT]
  Q6 = npn-Powertransistor [package="TO220 [THT]"]
  Q7 = npn-Powertransistor [package="TO220 [THT]"]
  R4 = Resistor [tolerance=±5% resistance=1.5k package=THT]
  R5 = Resistor [tolerance=±5% resistance=1.5k package=THT]
  R6 = Resistor [tolerance=±5% resistance=1.5k package=THT]
  U2 = AT42QT1012 [package=sot-23-6]  # not connected
  J2 = Screw terminal - 2 pins [package=THT]
  JP4 = Header 3 [package=screwterminal-3.5mm-3_lock.007s]
  JP3 = Header 4 [package=screwterminal-3.5mm-4_lock]

nets:
  5.1V: Adafruit_HUZZAH_ESP8266_Breakout1.GND, U1.GND, Q5.emitter, Q6.emitter, Q7.emitter, J2.pin2, JP4.2
  N1: Adafruit_HUZZAH_ESP8266_Breakout1.VBat, U1.output_voltage, JP4.1
  N2: Adafruit_HUZZAH_ESP8266_Breakout1.#13, R4.Pin_0
  N3: Adafruit_HUZZAH_ESP8266_Breakout1.#12, R6.Pin_0
  N4: Adafruit_HUZZAH_ESP8266_Breakout1.#14, R5.Pin_0
  N5: Adafruit_HUZZAH_ESP8266_Breakout1.#4, JP4.3
  GND: U1.input_voltage, J2.pin1, JP3.1
  N6: Q5.base, R4.Pin_1
  N7: Q5.collector, R1.Pin_0
  N8: R1.Pin_1, JP3.2
  N9: R2.Pin_0, Q6.collector
  N10: R2.Pin_1, JP3.4
  N11: R3.Pin_0, Q7.collector
  N12: R3.Pin_1, JP3.3
  N13: Q6.base, R5.Pin_1
  N14: Q7.base, R6.Pin_1

notes:
  g 2.2Ω
  r 3.3Ω
  b 2.2Ω
  apexskier smart light v0.0.1

// code stored in the sketch: light.ino
#include <ESP8266WiFi.h>
#include <ESP8266WebServer.h>
#include <ESP8266mDNS.h>
#include <WiFiUdp.h>
#include <TimeLib.h>
#include <TimeAlarms.h>
#include <limits.h>
// #include "private.h"
#include "color.h"

#define TOUCH_PIN 4
#define R_PIN 12
#define G_PIN 13
#define B_PIN 14
#define PWMRANGE_CUSTOM 255

// Define these in private.h
// const char* ssid     = "ssid";
// const char* password = "not my real password";

const char* ssid     = "☔️☁️";
const char* password = "reason maple speed junk";

// A UDP instance to let us send and receive packets over UDP
WiFiUDP udp;

// A webserver
ESP8266WebServer server(80);

void (*void_function)();

// Time syncronizing stuff (ntp.ino)
const int NTP_PACKET_SIZE = 48; // NTP time stamp is in the first 48 bytes of the message
byte packetBuffer[NTP_PACKET_SIZE]; //buffer to hold incoming and outgoing packets
void setupTime();
unsigned long sendNTPpacket(IPAddress& address);
void syncTimeStart();
void timeLoopCall();
void testColorSequence();

// Web server functions (server.ino)
void handle404();
void handleColor();
void handleOff();
void handleStartAlarm();
void handleSparkle();
void handleRainbow();
void handleStatus();
void handleRoot();

// LED manipulation over PWM
void startTransition(rgb_color to, unsigned long duration);
void startSunrise(unsigned long duration);
void startSparkling();
void startRainbow(unsigned long speed);
void wakeupAlarm();
void writeOff();
void writeColor(rgb_color color);
uint scaledPWM(float intensity);
uint linearPWM(float intensity);
void colorLoopCall();

// color transition
rgb_color transitionStartColor = {0, 0, 0};
rgb_color transitionEndColor = {0, 0, 0};
unsigned long transitionStartTime  = 0;
unsigned long transitionEndTime = 0;
unsigned long transitionSpeed = 0;
void touchLoopCall();

// lamp states
const int DIM_STATES = 6;
const int OFF_STATE = 0;
const int INVALID_STATE = -1;
const int SUNRISE_STATE = -2;
const int CUSTOM_STATE = -3;
const int SPARKLE_STATE = -4;
const int RAINBOW_STATE = -5;
int state = OFF_STATE;

// globals to handle touch sensor
int wasTouching = 0;
unsigned long touchStart = 0;
unsigned long nextTouch = 0;
unsigned long lastTouch = 0;
const unsigned long TOUCH_DELAY = 50; // poll for touches every 50 ms
const unsigned long LONG_TOUCH = 1000; // 1 second
const unsigned long STATE_DELAY = 5000; // turn off on new touches after 5 seconds

// global state of lamp -- should always be in sync with reality
rgb_color currentColor = {0, 0, 0};

// global time since reset, to avoid calling millis more than once a loop
unsigned long current_millis = 0;

void setup() {
  Serial.begin(115200);
  Serial.println();
  Serial.println();

  pinMode(TOUCH_PIN, INPUT);
  pinMode(R_PIN, OUTPUT);
  pinMode(G_PIN, OUTPUT);
  pinMode(B_PIN, OUTPUT);

  // Set PWM max to 255, to match color vals exactly. Easier processing
  analogWriteRange(PWMRANGE_CUSTOM);

  writeOff();
  delay(5000); // Wait a moment before starting up
  testColorSequence();

  // connecting to a WiFi network
  Serial.print("Connecting to ");
  Serial.println(ssid);
  WiFi.begin(ssid, password);

  while (WiFi.status() != WL_CONNECTED) {
    Alarm.delay(500);
    Serial.print(".");
  }
  Serial.println("");

  Serial.println("WiFi connected");
  Serial.print("IP address: ");
  Serial.println(WiFi.localIP());

  Serial.println("Starting UDP");
  udp.begin(2390); // start listening on this port
  Serial.print("Local port: ");
  Serial.println(udp.localPort());

  // ntp time sync
  setupTime();

  if (MDNS.begin("esp8266")) {
    Serial.println("MDNS responder started");
  }

  // webserver routing
  server.on("/", handleRoot);
  server.on("/status", handleStatus);
  server.on("/off", handleOff);
  server.on("/sunrise", handleStartAlarm);
  server.on("/sparkle", handleSparkle);
  server.on("/rainbow", handleRainbow);
  server.on("/color", handleColor);
  server.onNotFound(handle404);
  server.begin();
  Serial.println("HTTP server started");
}

void loop() {
  current_millis = millis();

  timeLoopCall(); // logic to update current time asyncronously
  touchLoopCall(); // logic to handle touches
  colorLoopCall(); // logic to fade between colors
  server.handleClient(); // webserver

  Alarm.delay(0); // allow alarm processing
}

void touchLoopCall() {
  // rate limit to once every TOUCH_DELAY
  if (current_millis > nextTouch) {
    nextTouch = current_millis + TOUCH_DELAY;

    int touching = digitalRead(TOUCH_PIN);

    // don't register multiple touches when the person's touch hasn't ended
    if (touching) {
      if (!wasTouching) {
        touchStart = current_millis;

        // if we're not in a dim state (e.g. sunrise) set off
        // this means lamp will turn off
        if (state < 0) {
          state = DIM_STATES - 1;
        }

        // increment state by one (loop down at max) unless it's been off for a while
        // then turn off
        state = int(current_millis <= lastTouch | state == OFF_STATE) * (state + 1) % DIM_STATES;
        byte intensity = byte((float(state) / float(DIM_STATES - 1)) * 255);
        rgb_color newColor = (rgb_color) {intensity, intensity, intensity};

        Serial.print("state: ");
        Serial.println(state);
        // fade to next dim level (or off)
        startTransition(newColor, 500);
      } else {
        if (current_millis - touchStart > LONG_TOUCH && state != OFF_STATE) {
          state = DIM_STATES - 1; // brightest
          startTransition({255, 255, 255}, 500);
        }
      }
    }

    // rate limiting
    if (touching) {
      lastTouch = current_millis + STATE_DELAY;
    }

    wasTouching = touching;
  }
}

void colorLoopCall() {
  // fade to next color without blocking
  if (transitionEndTime > current_millis) {
    unsigned long duration = transitionEndTime - transitionStartTime;
    float percent = float(current_millis - transitionStartTime) / duration;

    constrain(percent, 0, 1);

    rgb_color newColor;
    byte randByte;
    float hue;

    switch (state) {
    case SUNRISE_STATE:
      newColor = sunriseInterpolation(percent);
      if (percent == 1) {
        state = DIM_STATES - 1; // highest brightness
      }
      break;
    case SPARKLE_STATE:
      randByte = byte(random(100, 255));
      newColor = {randByte, randByte, randByte};
      break;
    case RAINBOW_STATE:
      hue = float(current_millis % transitionSpeed) / transitionSpeed;
      newColor = hsv_to_rgb({hue, 1, 1});
      Serial.print("rainbow: ");
      Serial.print(hue);
      Serial.print(", ");
      Serial.println(rgb_to_hex(newColor), HEX);
      break;
    default:
      newColor = interpolateColor(transitionStartColor, transitionEndColor, percent);

      Serial.print("transition: ");
      Serial.print(percent * 100);
      Serial.print("%, ");
      Serial.println(rgb_to_hex(newColor), HEX);
    }

    writeColor(newColor);
  } else if (!equals(transitionEndColor, currentColor)) {
    // ensure we always end on the end color, and don't stop early
    Serial.print("transition: ");
    Serial.print(100);
    Serial.print("%, ");
    Serial.println(rgb_to_hex(transitionEndColor), HEX);

    writeColor(transitionEndColor);
  }
}

void startTransition(rgb_color to, unsigned long duration) {
  transitionStartTime = current_millis;
  transitionEndTime = current_millis + duration;
  transitionStartColor = currentColor;
  transitionEndColor = to;
}

void startSunrise(unsigned long duration) {
  transitionStartTime = current_millis;
  transitionEndTime = current_millis + duration;
  state = SUNRISE_STATE;
  transitionStartColor = currentColor;
  transitionEndColor = {255, 255, 255};
  Serial.println("Started sunrise");
}

void startSparkling() {
  state = SPARKLE_STATE;
  transitionEndTime = ULONG_MAX;
}

void startRainbow(unsigned long speed) {
  state = RAINBOW_STATE;
  transitionSpeed = speed;
  transitionEndTime = ULONG_MAX;
}

// default sunrise
void wakeupAlarm() {
  Serial.println("Wake up!");
  startSunrise(1000 * 60 * 30);
}

void writeOff() {
  currentColor = {0, 0, 0};
  transitionEndTime = 0;
  analogWrite(R_PIN, /*PWMRANGE_CUSTOM - */0);
  analogWrite(G_PIN, /*PWMRANGE_CUSTOM - */0);
  analogWrite(B_PIN, /*PWMRANGE_CUSTOM - */0);
}

void writeColor(rgb_color color) {
  currentColor = color;
  analogWrite(R_PIN, /*PWMRANGE_CUSTOM - */scaledPWM(float(color.r) / 255));
  analogWrite(G_PIN, /*PWMRANGE_CUSTOM - */scaledPWM(float(color.g) / 255));
  analogWrite(B_PIN, /*PWMRANGE_CUSTOM - */scaledPWM(float(color.b) / 255));
}

uint scaledPWM(float intensity) {
  // PWMRANGE_CUSTOM should be 255
  return uint(double(PWMRANGE_CUSTOM) * pow(intensity, 2));
}

uint linearPWM(float intensity) {
  return uint(double(PWMRANGE_CUSTOM) * intensity);
}

void testColorSequence() {
  writeOff();

  writeColor(hex_to_rgb(0xff0000));
  delay(1000);
  writeColor(hex_to_rgb(0x00ff00));
  delay(1000);
  writeColor(hex_to_rgb(0x0000ff));
  delay(1000);

  writeColor(hex_to_rgb(0xffff00));
  delay(1000);
  writeColor(hex_to_rgb(0xff00ff));
  delay(1000);
  writeColor(hex_to_rgb(0x00ffff));
  delay(1000);

  writeColor(hex_to_rgb(0xffffff));
  delay(200);
  writeColor(hex_to_rgb(0xcccccc));
  delay(200);
  writeColor(hex_to_rgb(0x999999));
  delay(200);
  writeColor(hex_to_rgb(0x666666));
  delay(200);
  writeColor(hex_to_rgb(0x333333));
  delay(200);
  writeColor(hex_to_rgb(0x000000));
  delay(200);

  writeOff();
}
